# Fritzing sketch NANO-TRAY (saved by Fritzing 0.9.3b)

parts:
  NANO = Arduino Nano (Rev3.0) (ICSP)
  RL1-2 = 2-Channel 5v Relay Shield [package=relay-2ch5v10a]
  RL3-4 = 2-Channel 5v Relay Shield [package=relay-2ch5v10a]
  RL5-6 = 2-Channel 5v Relay Shield [package=relay-2ch5v10a]
  RL7-8 = 2-Channel 5v Relay Shield [package=relay-2ch5v10a]
  IR1 = TSOP312.., 314.. [package=THT]
  TRAIN_DC_MOTOR = DC Motor
  IC1 = Voltage Regulator [package=to220-igo]
  C1 = Capacitor Polarized [package=nippon_f80]
  C2 = Capacitor Polarized [package=nippon_f80]
  L298 = H-Bridge with L298N
  +12VDC = BANANA_CONN [package=banana_conn]
  GND = BANANA_CONN [package=banana_conn]
  J3 = BANANA_CONN [package=banana_conn]
  J4 = BANANA_CONN [package=banana_conn]
  EXCH1 = SWITCH_SPDT [package=kps-1290]
  EXCH2 = SWITCH_SPDT [package=kps-1290]
  EXCH3 = SWITCH_SPDT [package=kps-1290]
  EXCH4 = SWITCH_SPDT [package=kps-1290]

nets:
  GND: NANO.GND, RL1-2.GND, RL3-4.GND, RL5-6.GND, RL7-8.GND, IR1.GND, L298.GND
  N1: NANO.D2, RL1-2.IN1
  N2: NANO.D3, RL1-2.IN2
  N3: NANO.D4, RL3-4.IN1
  N4: NANO.D5, RL3-4.IN2
  N5: NANO.D6, RL5-6.IN1
  N6: NANO.D7, RL5-6.IN2
  N7: NANO.D8, RL7-8.IN1
  N8: NANO.D9, L298.ENA, L298.ENB
  N9: NANO.D10, IR1.Data
  N10: NANO.D11/MOSI, RL7-8.IN2
  N11: NANO.D12/MISO, L298.IN1, L298.IN4
  VIN: NANO.VIN, L298.12V
  N12: NANO.D13/SCK, L298.IN2, L298.IN3
  N13: RL1-2.K1-In, EXCH1.O
  N14: RL1-2.K1-Off, RL1-2.K2-Off, RL3-4.K1-Off, RL3-4.K2-Off, RL5-6.K1-Off, RL5-6.K2-Off, RL7-8.K1-Off, RL7-8.K2-Off, J4.1
  N15: RL1-2.K2-In, EXCH1.S
  N16: RL3-4.K1-In, EXCH2.O
  N17: RL3-4.K2-In, EXCH2.S
  VCC: RL5-6.VCC, RL7-8.VCC
  N18: RL5-6.K1-In, EXCH3.O
  N19: RL5-6.K2-In, EXCH3.S
  N20: RL7-8.K1-In, EXCH4.O
  N21: RL7-8.K2-In, EXCH4.S
  N22: IR1.Vs, IC1.OUT, C2.+
  N23: TRAIN_DC_MOTOR.pin_1, L298.M1-02
  N24: TRAIN_DC_MOTOR.pin_2, L298.M1-01
  N25: IC1.GND, C1.+, +12VDC.1
  N26: IC1.IN, C1.-, C2.-, GND.1
  N27: J3.1, EXCH1.P, EXCH2.P, EXCH3.P, EXCH4.P

notes:
  Exchange Supply (AC or DC)

custom parts:
  2-Channel 5v Relay Shield: 2 Channel 5v Relay Shield w. 2x SPD-06VDC-SD-C
  H-Bridge with L298N: h-bridge
